# Fritzing sketch ledPattern (saved by Fritzing 0.9.3b)

parts:
  LED16 = LED - 5mm [color="Green (560nm)" package="5 mm [THT]"]
  LED61 = LED - 5mm [color="Green (560nm)" package="5 mm [THT]"]
  LED10 = LED - 5mm [color="Green (560nm)" package="5 mm [THT]"]
  LED46 = LED - 5mm [color="Green (560nm)" package="5 mm [THT]"]
  LED42 = LED - 5mm [color="Green (560nm)" package="5 mm [THT]"]
  LED39 = LED - 5mm [color="Green (560nm)" package="5 mm [THT]"]
  LED19 = LED - 5mm [color="Green (560nm)" package="5 mm [THT]"]
  LED32 = LED - 5mm [color="Green (560nm)" package="5 mm [THT]"]
  LED23 = LED - 5mm [color="Green (560nm)" package="5 mm [THT]"]
  LED64 = LED - 5mm [color="Green (560nm)" package="5 mm [THT]"]
  LED53 = LED - 5mm [color="Green (560nm)" package="5 mm [THT]"]
  LED14 = LED - 5mm [color="Green (560nm)" package="5 mm [THT]"]
  LED44 = LED - 5mm [color="Green (560nm)" package="5 mm [THT]"]
  LED35 = LED - 5mm [color="Green (560nm)" package="5 mm [THT]"]
  LED41 = LED - 5mm [color="Green (560nm)" package="5 mm [THT]"]
  LED25 = LED - 5mm [color="Green (560nm)" package="5 mm [THT]"]
  LED11 = LED - 5mm [color="Green (560nm)" package="5 mm [THT]"]
  LED2 = LED - 5mm [color="Green (560nm)" package="5 mm [THT]"]
  LED55 = LED - 5mm [color="Green (560nm)" package="5 mm [THT]"]
  LED59 = LED - 5mm [color="Green (560nm)" package="5 mm [THT]"]
  LED22 = LED - 5mm [color="Green (560nm)" package="5 mm [THT]"]
  LED50 = LED - 5mm [color="Green (560nm)" package="5 mm [THT]"]
  Part1 = Arduino Uno (Rev3) - ICSP
  LED48 = LED - 5mm [color="Green (560nm)" package="5 mm [THT]"]
  LED1 = LED - 5mm [color="Green (560nm)" package="5 mm [THT]"]
  LED38 = LED - 5mm [color="Green (560nm)" package="5 mm [THT]"]
  LED20 = LED - 5mm [color="Green (560nm)" package="5 mm [THT]"]
  LED52 = LED - 5mm [color="Green (560nm)" package="5 mm [THT]"]
  LED7 = LED - 5mm [color="Green (560nm)" package="5 mm [THT]"]
  LED60 = LED - 5mm [color="Green (560nm)" package="5 mm [THT]"]
  LED34 = LED - 5mm [color="Green (560nm)" package="5 mm [THT]"]
  LED5 = LED - 5mm [color="Green (560nm)" package="5 mm [THT]"]
  LED17 = LED - 5mm [color="Green (560nm)" package="5 mm [THT]"]
  LED57 = LED - 5mm [color="Green (560nm)" package="5 mm [THT]"]
  LED12 = LED - 5mm [color="Green (560nm)" package="5 mm [THT]"]
  LED43 = LED - 5mm [color="Green (560nm)" package="5 mm [THT]"]
  LED15 = LED - 5mm [color="Green (560nm)" package="5 mm [THT]"]
  LED28 = LED - 5mm [color="Green (560nm)" package="5 mm [THT]"]
  LED8 = LED - 5mm [color="Green (560nm)" package="5 mm [THT]"]
  LED3 = LED - 5mm [color="Green (560nm)" package="5 mm [THT]"]
  LED30 = LED - 5mm [color="Green (560nm)" package="5 mm [THT]"]
  LED62 = LED - 5mm [color="Green (560nm)" package="5 mm [THT]"]
  LED26 = LED - 5mm [color="Green (560nm)" package="5 mm [THT]"]
  LED63 = LED - 5mm [color="Green (560nm)" package="5 mm [THT]"]
  LED6 = LED - 5mm [color="Green (560nm)" package="5 mm [THT]"]
  LED37 = LED - 5mm [color="Green (560nm)" package="5 mm [THT]"]
  LED9 = LED - 5mm [color="Green (560nm)" package="5 mm [THT]"]
  LED18 = LED - 5mm [color="Green (560nm)" package="5 mm [THT]"]
  LED51 = LED - 5mm [color="Green (560nm)" package="5 mm [THT]"]
  LED13 = LED - 5mm [color="Green (560nm)" package="5 mm [THT]"]
  LED36 = LED - 5mm [color="Green (560nm)" package="5 mm [THT]"]
  LED27 = LED - 5mm [color="Green (560nm)" package="5 mm [THT]"]
  LED45 = LED - 5mm [color="Green (560nm)" package="5 mm [THT]"]
  LED21 = LED - 5mm [color="Green (560nm)" package="5 mm [THT]"]
  LED33 = LED - 5mm [color="Green (560nm)" package="5 mm [THT]"]
  LED4 = LED - 5mm [color="Green (560nm)" package="5 mm [THT]"]
  LED56 = LED - 5mm [color="Green (560nm)" package="5 mm [THT]"]
  LED40 = LED - 5mm [color="Green (560nm)" package="5 mm [THT]"]
  LED54 = LED - 5mm [color="Green (560nm)" package="5 mm [THT]"]
  LED24 = LED - 5mm [color="Green (560nm)" package="5 mm [THT]"]
  LED58 = LED - 5mm [color="Green (560nm)" package="5 mm [THT]"]
  LED31 = LED - 5mm [color="Green (560nm)" package="5 mm [THT]"]
  LED29 = LED - 5mm [color="Green (560nm)" package="5 mm [THT]"]
  LED47 = LED - 5mm [color="Green (560nm)" package="5 mm [THT]"]
  LED49 = LED - 5mm [color="Green (560nm)" package="5 mm [THT]"]

nets:
  N1: LED16.cathode, LED10.cathode, LED14.cathode, LED11.cathode, LED2.cathode, Part1.A5/SCL, Part1.ICSP_SCK, Part1.ICSP_MOSI, Part1.D8, Part1.D9_PWM, Part1.D10_PWM/SS, Part1.D11_PWM/MOSI, Part1.D12/MISO, Part1.D13/SCK, Part1.D0/RX, Part1.D1/TX, Part1.D2, Part1.D3_PWM, Part1.D4, Part1.D5_PWM, Part1.D6_PWM, Part1.D7, LED1.cathode, LED7.cathode, LED5.cathode, LED12.cathode, LED15.cathode, LED8.cathode, LED3.cathode, LED6.cathode, LED9.cathode, LED13.cathode, LED4.cathode
  N2: LED16.anode, LED10.anode, LED14.anode, LED11.anode, LED2.anode, Part1.A0, LED1.anode, LED7.anode, LED5.anode, LED12.anode, LED15.anode, LED8.anode, LED3.anode, LED6.anode, LED9.anode, LED13.anode, LED4.anode
  N3: LED61.cathode, LED64.cathode, LED53.cathode, LED55.cathode, LED59.cathode, LED50.cathode, LED52.cathode, LED60.cathode, LED57.cathode, LED62.cathode, LED63.cathode, LED51.cathode, LED56.cathode, LED54.cathode, LED58.cathode, LED49.cathode
  N4: LED61.anode, LED64.anode, LED53.anode, LED55.anode, LED59.anode, LED50.anode, Part1.A3, LED52.anode, LED60.anode, LED57.anode, LED62.anode, LED63.anode, LED51.anode, LED56.anode, LED54.anode, LED58.anode, LED49.anode
  N5: LED46.cathode, LED42.cathode, LED39.cathode, LED44.cathode, LED35.cathode, LED41.cathode, LED48.cathode, LED38.cathode, LED34.cathode, LED43.cathode, LED37.cathode, LED36.cathode, LED45.cathode, LED33.cathode, LED40.cathode, LED47.cathode
  N6: LED46.anode, LED42.anode, LED39.anode, LED44.anode, LED35.anode, LED41.anode, Part1.A2, LED48.anode, LED38.anode, LED34.anode, LED43.anode, LED37.anode, LED36.anode, LED45.anode, LED33.anode, LED40.anode, LED47.anode
  N7: LED19.cathode, LED32.cathode, LED23.cathode, LED25.cathode, LED22.cathode, LED20.cathode, LED17.cathode, LED28.cathode, LED30.cathode, LED26.cathode, LED18.cathode, LED27.cathode, LED21.cathode, LED24.cathode, LED31.cathode, LED29.cathode
  N8: LED19.anode, LED32.anode, LED23.anode, LED25.anode, LED22.anode, Part1.A1, LED20.anode, LED17.anode, LED28.anode, LED30.anode, LED26.anode, LED18.anode, LED27.anode, LED21.anode, LED24.anode, LED31.anode, LED29.anode

notes:
  Layer 4
  Layer 3
  Layer 2
  Layer 1
  positive
  negative
  Copyleft (c) Isaac Arcilla 2017
  MIT License

// code stored in the sketch: Untitled.ino

int layer[4]={A3,A2,A1,A0};
int led[16]={13,12,11,10,9,8,7,6,5,4,3,2,1,0,A5,A4};
int time = 250;
 
void setup()
{
  for(int i = 0; i<16; i++)
  {
    pinMode(led[i], OUTPUT);
  }
  for(int i = 0; i<4; i++)
  {
    pinMode(layer[i], OUTPUT);
  }
  randomSeed(analogRead(10));
}


void loop()
{
  turnEverythingOff();
  randomflicker();
  randomRain();
  goThroughAllLedsOneAtATime();
  turnEverythingOff();
  delay(2000);
}

void turnEverythingOff()
 {
   for(int i = 0; i<16; i++)
   {
     digitalWrite(led[i], 1);
   }
   for(int i = 0; i<4; i++)
   {
     digitalWrite(layer[i], 0);
   }
 }
 
void turnEverythingOn()
{
  for(int i = 0; i<16; i++)
  {
    digitalWrite(led[i], 0);
  }
  //turning on layers
  for(int i = 0; i<4; i++)
  {
    digitalWrite(layer[i], 1);
  }
}
void randomflicker()
{
  turnEverythingOff();
  int x = 10;
  for(int i = 0; i !=750; i+=2)
  {
  int randomLayer = random(0,4);
  int randomLed = random(0,16);
  
  digitalWrite(layer[randomLayer], 1);
  digitalWrite(led[randomLed], 0);
  delay(x);
  digitalWrite(layer[randomLayer], 0);
  digitalWrite(led[randomLed], 1);
  delay(x); 
  }
}
void randomRain()
{
  turnEverythingOff();
  int x = 100;
  for(int i = 0; i!=60; i+=2)
  {
    int randomLed = random(0,16);
    digitalWrite(led[randomLed], 0);
    digitalWrite(layer[3], 1);
    delay(x+50);
    digitalWrite(layer[3], 0);
    digitalWrite(layer[2], 1);
    delay(x);
    digitalWrite(layer[2], 0);
    digitalWrite(layer[1], 1);
    delay(x);
    digitalWrite(layer[1], 0);
    digitalWrite(layer[0], 1);
    delay(x+50);
    digitalWrite(layer[0], 0);
    digitalWrite(led[randomLed], 1);
  }
}
void goThroughAllLedsOneAtATime()
{
  int x = 15;
  turnEverythingOff();
  for(int y = 0; y<5; y++)
  {
    //0-3
    for(int count = 4; count != 0; count--)
    {
      digitalWrite(layer[count-1], 1);
      for(int i = 0; i<4; i++)
      {
        digitalWrite(led[i], 0);
        delay(x);
        digitalWrite(led[i], 1);
        delay(x);
      }
    digitalWrite(layer[count-1], 0);
    }
    //4-7
    for(int count = 0; count < 4; count++)
    {
      digitalWrite(layer[count], 1);
      for(int i = 4; i<8; i++)
      {
        digitalWrite(led[i], 0);
        delay(x);
        digitalWrite(led[i], 1);
        delay(x);
      }
    digitalWrite(layer[count], 0);
    }
    //8-11
    for(int count = 4; count != 0; count--)
    {
      digitalWrite(layer[count-1], 1);
      for(int i = 8; i<12; i++)
      {
        digitalWrite(led[i], 0);
        delay(x);
        digitalWrite(led[i], 1);
        delay(x);
      }
    digitalWrite(layer[count-1], 0);
    }
    //12-15
    for(int count = 0; count < 4; count++)
    {
      digitalWrite(layer[count], 1);
      for(int i = 12; i<16; i++)
      {
        digitalWrite(led[i], 0);
        delay(x);
        digitalWrite(led[i], 1);
        delay(x);
      }
    digitalWrite(layer[count], 0);
    }
  }
}
